# Fritzing sketch sketch (saved by Fritzing 1.0.1rc)
# 18650 Li-ion Battery: CC-BY Dr Kristofer Chan, King's College London/Remote-research.org
circuit board: 8.46667cm x 5.64444cm
breadboards: 1

parts:
  DFRobot_DFPlayer_Mini1 = DFRobot DFPlayer Mini [part_number=DFR0299]
  A1 = Esp32-c3 super mini
  S1 = Round Pushbutton
  SP1 = SPEAKER [package=pcb_mount_speaker]
  Bauteil1 = Pololu 5V Step-Up Regulator
  TP1 = TP4056 [chip_label=TP4056 package="DIP (Dual Inline) [THT]"]
  BAT1 = 18650 Li-ion Battery [package=battery-18650]
  BAT2 = 18650 Li-ion Battery [package=battery-18650]
  S2 = Square Pushbutton

nets:
  N1: DFRobot_DFPlayer_Mini1.VCC, A1.Pin_16, Bauteil1.VOUT
  N2: DFRobot_DFPlayer_Mini1.RX, A1.Pin_8
  N3: DFRobot_DFPlayer_Mini1.TX, A1.Pin_7
  N4: DFRobot_DFPlayer_Mini1.SPK_1, SP1.-
  N5: DFRobot_DFPlayer_Mini1.GND-1, DFRobot_DFPlayer_Mini1.GND-2, A1.Pin_15, S1.leg1, Bauteil1.GND, TP1.pin6
  N6: DFRobot_DFPlayer_Mini1.SPK_2, SP1.+
  N7: DFRobot_DFPlayer_Mini1.BUSY, A1.Pin_6
  N8: A1.Pin_13, S1.leg0
  N9: Bauteil1.VIN, TP1.pin3
  N10: TP1.pin4, BAT1.+, BAT2.+
  N11: TP1.pin5, S2.leg1
  N12: BAT1.-, BAT2.-, S2.leg0

notes:
  der button ist die Wählscheibe
  der Lautsprecher des Telefonhörers
  der button ist die Gabel, schließt beim Abheben

custom parts:
  Esp32-c3 super mini: ESP32-C3 Development Board ESP32 SuperMini Development Board ESP32 Development Board WiFi Bluetooth.
  TP4056: A DIP stand-in part for whatever IC you want. With 6 pins on a 300mil dual inline package (DIP) footprint.
  18650 Li-ion Battery: 18650 li-ion Battery Standard 18650 battery with interactive connectors Creative Common Attribution 4.0 International (CC-BY 4.0) license. Any use of this part requires attribution of Dr Kristofer Chan, Department of Geography, King's College London. Contact kristofer.chan [at] kcl.ac.uk OR kris [at] remote-research.org for further information.
